# Fritzing sketch receiver_diagram (saved by Fritzing 0.9.3b)

parts:
  M1 = DOIT Esp32 DevKit v1 (30 pins long, 11 pins width) [part_number=ESP32S-PIN30]
  S1 = H-Bridge with L298N
  M2 = DC Motor  # not connected
  M3 = DC Motor
  M4 = DC Motor  # not connected
  M5 = DC Motor

nets:
  N1: M1.D5, S1.IN1
  N2: M1.D18, S1.IN2
  N3: M1.D19, S1.IN3
  N4: M1.D21, S1.IN4
  GND: M1.GND, S1.GND
  VIN: M1.VIN, S1.5V
  N5: S1.ENA, S1.ENA-5V
  N6: S1.ENB, S1.ENB-5V
  N7: S1.M1-01, M3.pin_1, M5.pin_1
  N8: S1.M1-02, M3.pin_2, M5.pin_2

notes:
  12V DC Supply

custom parts:
  DOIT Esp32 DevKit v1 (30 pins long, 11 pins width): The DOIT Esp32 DevKit v1 is one of the development board created by DOIT to evaluate the ESP-WROOM-32 module. It is based on the ESP32 microcontroller that boasts Wifi, Bluetooth, Ethernet and Low Power support all in a single chip. (vanepp) made breadboard work, adjusted pin numbering and labels and reduced size of schematic and cleaned up pcb. This chip is 30pins long (2 x15) and 11 pins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
  H-Bridge with L298N: h-bridge
